// Logisim project controlunit_Project.circ as structural Verilog: 1 circuit, main circuit main
module main (
  input  go,
  input  gt,
  input  lt_eq,
  input  CLK,
  output LR,
  output R_M,
  output Lb,
  output La,
  output S__1_B,
  output S_A_M,
  output LM,
  output Sa
);

  wire N0_2_out, N0_3_out, N0_4_out, N1_2_out, N1_3_out, N1_out, N2_3_out, N2_4_out, N2_5_out, not_1_out,
       not_2_out, not_3_out, or_out, S3_out, S5_out, S6_out, xor_1_out;
  wire [2:0] N0_out, register_1_q;

  Register #(.width(3)) register_1 (.D(N0_out), .en(1'b1), .Q(register_1_q), .clk(CLK));  // open: clr
  or \or  (or_out, gt, lt_eq);
  or N2 (N0_out[2], N2_3_out, N2_4_out, N2_5_out);
  or N2_2 (N0_out[1], N1_out, N1_2_out, N1_3_out);
  or N0 (N0_out[0], N0_2_out, N0_3_out, N0_4_out);
  and N2_3 (N2_3_out, not_3_out, register_1_q[1], not_1_out, lt_eq);
  and N2_4 (N2_4_out, not_3_out, register_1_q[1], register_1_q[0]);
  and N2_5 (N2_5_out, register_1_q[2], not_2_out);
  and N1 (N1_out, not_3_out, not_2_out, register_1_q[0]);
  and N1_2 (N1_2_out, not_3_out, register_1_q[1], not_1_out, or_out);
  and N1_3 (N1_3_out, register_1_q[2], xor_1_out);
  and N0_2 (N0_2_out, not_1_out, not_2_out, not_3_out, go);
  and N0_3 (N0_3_out, not_3_out, not_1_out, register_1_q[1], or_out);
  and N0_4 (N0_4_out, not_1_out, not_2_out, register_1_q[2]);
  xor xor_1 (xor_1_out, register_1_q[0], register_1_q[1]);
  not not_1 (not_1_out, register_1_q[0]);
  not not_2 (not_2_out, register_1_q[1]);
  not not_3 (not_3_out, register_1_q[2]);
  and S7 (LR, register_1_q[1], register_1_q[2], register_1_q[0]);
  and S1 (Lb, register_1_q[0], not_2_out, not_3_out);
  and S3 (S3_out, register_1_q[0], register_1_q[1], not_3_out);
  and S4 (LM, register_1_q[2], not_2_out, not_1_out);
  and S6 (S6_out, register_1_q[2], register_1_q[1], not_1_out);
  and S5 (S5_out, register_1_q[0], not_2_out, register_1_q[2]);
  or or_2 (S__1_B, S3_out, LM);
  or u_S_A_M (S_A_M, S3_out, LM);
  or N2_6 (Sa, S6_out, S5_out);
  or u_la (La, Lb, S6_out);

  assign R_M = Lb;

  // Notes on the sheet:
  //   S0'
  //   S1'
  //   S2'
  //   S0'
  //   S1'
  //   S2'
endmodule
