// Logisim project datapath_PROJECT.circ as structural Verilog: 1 circuit, main circuit main
module main (
  input  S_A,
  input  [15:0] A_i,
  input  L_A,
  input  [15:0] B_i,
  input  L_R,
  input  L_b,
  input  CLK,
  input  S__1_B,
  input  L_M,
  input  S_A_M,
  input  R_M,
  output gt,
  output [15:0] Res,
  output lt_eq
);

  wire comparator_1_eq, comparator_1_lt;
  wire [15:0] A_q, adder_1_out, B_q, MULT_q, multiplexer_1_out, multiplexer_2_out, multiplexer_3_out;

  Multiplexer #(.width(16), .enable("false")) multiplexer_1 (
    .in0(A_i), .in1(adder_1_out), .out(multiplexer_1_out), .sel(S_A));
  Register #(.width(16)) A (.D(multiplexer_1_out), .en(L_A), .Q(A_q), .clk(CLK));  // open: clr
  Register #(.width(16)) B (.D(B_i), .en(L_b), .Q(B_q), .clk(CLK));  // open: clr
  Register #(.width(16)) MULT (.D(adder_1_out), .en(L_M), .Q(MULT_q), .clk(CLK), .clr(R_M));
  Comparator #(.width(16)) comparator_1 (.a(A_q), .b({16{1'b0}}), .gt(gt), .eq(comparator_1_eq), .lt(comparator_1_lt));
  Multiplexer #(.width(16), .enable("false")) multiplexer_2 (
    .in0({16{1'b1}}), .in1(B_q), .out(multiplexer_2_out), .sel(S__1_B));
  Multiplexer #(.width(16), .enable("false")) multiplexer_3 (
    .in0(A_q), .in1(MULT_q), .out(multiplexer_3_out), .sel(S_A_M));
  or u_lt_eq (lt_eq, comparator_1_eq, comparator_1_lt);
  Adder #(.width(16)) adder_1 (.a(multiplexer_2_out), .b(multiplexer_3_out), .out(adder_1_out));  // open: cin, cout
  Register #(.width(16)) u_Res (.D(MULT_q), .en(L_R), .Q(Res), .clk(CLK));  // open: clr

  // Notes on the sheet:
  //   0
  //   -1
endmodule
