// Logisim project works_PROJECT.circ as structural Verilog: 1 circuit, main circuit main
module main (
  input  [15:0] Bi,
  input  [15:0] Ai,
  output [15:0] RES
);

  wire button_1_out, clock_1_out, main_1_la, main_1_lb, main_1_lm, main_1_lr, main_1_r_m, main_1_s__1_b,
       main_1_s_a_m, main_1_sa, main_2_gt, main_2_lt_eq;

  Button button_1 (.out(button_1_out));
  Clock clock_1 (.out(clock_1_out));
  controlunit_Project_main main_1 (
    .go(button_1_out), .gt(main_2_gt), .lt_eq(main_2_lt_eq), .CLK(clock_1_out), .LR(main_1_lr),
    .R_M(main_1_r_m), .Lb(main_1_lb), .La(main_1_la), .S__1_B(main_1_s__1_b), .S_A_M(main_1_s_a_m),
    .LM(main_1_lm), .Sa(main_1_sa));
  datapath_PROJECT_main main_2 (
    .S_A(main_1_sa), .A_i(Ai), .L_A(main_1_la), .B_i(Bi), .L_R(main_1_lr), .L_b(main_1_lb),
    .CLK(clock_1_out), .L_M(main_1_lm), .R_M(main_1_r_m), .S__1_B(main_1_s__1_b), .S_A_M(main_1_s_a_m),
    .gt(main_2_gt), .Res(RES), .lt_eq(main_2_lt_eq));
endmodule
